// Logisim project alu.circ as structural Verilog: 11 circuits, main circuit main
module main (
  input  [15:0] X,
  input  [15:0] Y,
  input  [3:0] Switch__S,
  output Signed_Overflow,
  output [15:0] RESULT,
  output Equal
);

  wire add, addp8, sub, subp8;
  wire [15:0] add_output, addp8_output, and_out, or_out, sllv_out_3, slt_out_3, srav_out_3, srlv_out_3,
       sub_output, subp8_output;

  add u_add (.input_X(X), .input_Y(Y), .Output(add_output), .signed_overflow(add));  // open: unsigned_overflow
  sub u_sub (.input_X(X), .input_Y(Y), .Output(sub_output), .signed_overflow(sub));  // open: unsigned_overflow
  sllv sllv (.X(X), .Y(Y), .out_3(sllv_out_3));
  srlv srlv (.X(X), .Y(Y), .out_3(srlv_out_3));
  srav srav (.X(X), .Y(Y), .out_3(srav_out_3));
  slt slt (.in_1(X), .in_2(Y), .out_3(slt_out_3));
  assign or_out = X | Y;  // OR_Gate or, 16 bits wide
  assign and_out = X & Y;  // AND_Gate and, 16 bits wide
  addp8 u_addp8 (.input_X(X), .input_Y(Y), .Output(addp8_output), .Signed_Overflow(addp8));  // open: Unsigned_Overflow
  subp8 u_subp8 (.input_X(X), .input_Y(Y), .Output(subp8_output), .Signed_Overflow(subp8));  // open: Unsigned_Overflow
  Multiplexer #(.select(4), .width(16)) multiplexer_1 (
    .in0(add_output), .in1(sub_output), .in2(sllv_out_3), .in3(srlv_out_3), .in4(srav_out_3),
    .in5(slt_out_3), .in6(or_out), .in7(and_out), .in8(addp8_output), .in9(subp8_output), .out(RESULT),
    .sel(Switch__S));  // open: in10, in11, in12, in13, in14, in15, en
  Multiplexer #(.select(4)) multiplexer_2 (
    .in0(add), .in1(sub), .in2(1'b0), .in3(1'b0), .in4(1'b0), .in5(1'b0), .in6(1'b0), .in7(1'b0),
    .in8(addp8), .in9(subp8), .in10(1'b0), .in11(1'b0), .in12(1'b0), .in13(1'b0), .in14(1'b0), .in15(1'b0),
    .out(Signed_Overflow), .sel(Switch__S));  // open: en
  Comparator #(.width(16)) comparator_1 (.a(X), .b(Y), .eq(Equal));  // open: gt, lt

  // Other names for the same wires on the sheet: out = Signed_Overflow; switch[3:0] = Switch__S

  // Notes on the sheet:
  //   INPUT to your circuit
  //   INPUTS to your circuit
  //   DON'T CHANGE THE INPUTS AND OUTPUTS! IF YOU DO SO, YOU NEED TO MAKE SURE THE PINS ARE IN THE RIGHT PLACES!
  //   OUTPUTS of your circuit
endmodule

module sllv (
  input  [15:0] X,
  input  [15:0] Y,
  output [15:0] out_3
);

  Shifter #(.width(16)) shifter_1 (.in(X), .\dist (Y[3:0]), .out(out_3));
endmodule

module srlv (
  input  [15:0] X,
  input  [15:0] Y,
  output [15:0] out_3
);

  Shifter #(.width(16), .shift("lr")) shifter_1 (.in(X), .\dist (Y[3:0]), .out(out_3));
endmodule

module srav (
  input  [15:0] X,
  input  [15:0] Y,
  output [15:0] out_3
);

  Shifter #(.width(16), .shift("ar")) shifter_1 (.in(X), .\dist (Y[3:0]), .out(out_3));
endmodule

module slt (
  input  [15:0] in_1,
  input  [15:0] in_2,
  output [15:0] out_3
);

  Comparator #(.width(16)) comparator_1 (.a(in_1), .b(in_2), .lt(out_3[0]));  // open: gt, eq

  assign out_3[15:1] = {15{1'b0}};
endmodule

module addp8 (
  input  [15:0] input_X,
  input  [15:0] input_Y,
  output [15:0] Output,
  output Unsigned_Overflow,
  output Signed_Overflow
);

  wire a_overflow_signed_overflow, adder_1_cout, adder_2_cout, b_overflow_signed_overflow;

  Adder adder_1 (.a(input_X[7:0]), .b(input_Y[7:0]), .out(Output[7:0]), .cout(adder_1_cout));  // open: cin
  Adder adder_2 (.a(input_X[15:8]), .b(input_Y[15:8]), .out(Output[15:8]), .cout(adder_2_cout));  // open: cin
  check_overflow_sub a_overflow (
    .m_sig_fit_A(input_Y[7]), .m_sig_bit_B(input_X[7]), .m_sig_bit_Out(Output[7]),
    .signed_overflow(a_overflow_signed_overflow));
  or or_1 (Unsigned_Overflow, adder_1_cout, adder_2_cout);
  check_overflow_sub b_overflow (
    .m_sig_fit_A(input_X[15]), .m_sig_bit_B(input_Y[15]), .m_sig_bit_Out(Output[15]),
    .signed_overflow(b_overflow_signed_overflow));
  or or_2 (Signed_Overflow, a_overflow_signed_overflow, b_overflow_signed_overflow);
endmodule

module subp8 (
  input  [15:0] input_X,
  input  [15:0] input_Y,
  output [15:0] Output,
  output Unsigned_Overflow,
  output Signed_Overflow
);

  wire a_overflow_signed_overflow, b_overflow_signed_overflow, subtractor_1_bout, subtractor_2_bout;

  Subtractor subtractor_1 (
    .a(input_X[7:0]), .b(input_Y[7:0]), .out(Output[7:0]), .bout(subtractor_1_bout));  // open: bin
  Subtractor subtractor_2 (
    .a(input_X[15:8]), .b(input_Y[15:8]), .out(Output[15:8]), .bout(subtractor_2_bout));  // open: bin
  check_overflow_sub a_overflow (
    .m_sig_fit_A(input_Y[7]), .m_sig_bit_B(input_X[7]), .m_sig_bit_Out(Output[7]),
    .signed_overflow(a_overflow_signed_overflow));
  or or_1 (Unsigned_Overflow, subtractor_1_bout, subtractor_2_bout);
  check_overflow_sub b_overflow (
    .m_sig_fit_A(input_X[15]), .m_sig_bit_B(input_Y[15]), .m_sig_bit_Out(Output[15]),
    .signed_overflow(b_overflow_signed_overflow));
  or or_2 (Signed_Overflow, a_overflow_signed_overflow, b_overflow_signed_overflow);
endmodule

module add (
  input  [15:0] input_X,
  input  [15:0] input_Y,
  output [15:0] Output,
  output unsigned_overflow,
  output signed_overflow
);

  wire xnor_1_out, xor_1_out;

  Adder #(.width(16)) adder_1 (.a(input_X), .b(input_Y), .out(Output), .cout(unsigned_overflow));  // open: cin
  xnor xnor_1 (xnor_1_out, input_X[15], input_Y[15]);
  xor xor_1 (xor_1_out, Output[15], input_X[15]);
  and and_1 (signed_overflow, xor_1_out, xnor_1_out);

  // Other names for the same wires on the sheet: u_o = unsigned_overflow
endmodule

module sub (
  input  [15:0] input_X,
  input  [15:0] input_Y,
  output [15:0] Output,
  output unsigned_overflow,
  output signed_overflow
);

  wire xnor_1_out, xor_1_out;

  Subtractor #(.width(16)) subtractor_1 (
    .a(input_X), .b(input_Y), .out(Output), .bout(unsigned_overflow));  // open: bin
  xnor xnor_1 (xnor_1_out, input_X[15], input_Y[15]);
  xor xor_1 (xor_1_out, Output[15], input_X[15]);
  and and_1 (signed_overflow, xor_1_out, xnor_1_out);

  // Other names for the same wires on the sheet: u_o = unsigned_overflow
endmodule

module check_overflow (
  input  m_sig_bit_A,
  input  m_sig_bit_B,
  input  m_sig_bit_Out,
  output signed_overflow
);

  wire and_1_out, and_2_out, and_3_out, and_4_out, and_5_out, not_1_out, not_2_out, not_3_out;

  not not_1 (not_1_out, m_sig_bit_A);
  and and_1 (and_1_out, not_1_out, not_2_out);
  not not_2 (not_2_out, m_sig_bit_B);
  and and_2 (and_2_out, m_sig_bit_A, m_sig_bit_A);
  and and_3 (and_3_out, and_2_out, m_sig_bit_Out);
  not not_3 (not_3_out, m_sig_bit_Out);
  and and_4 (and_4_out, and_1_out, m_sig_bit_Out);
  and and_5 (and_5_out, and_3_out, not_3_out);
  or or_1 (signed_overflow, and_4_out, and_5_out);
endmodule

module check_overflow_sub (
  input  m_sig_fit_A,
  input  m_sig_bit_B,
  input  m_sig_bit_Out,
  output signed_overflow
);

  wire comparator_1_eq, not_1_out, xor_1_out;

  xor xor_1 (xor_1_out, m_sig_fit_A, m_sig_bit_B);
  Comparator #(.width(1)) comparator_1 (.a(m_sig_fit_A), .b(m_sig_bit_Out), .eq(comparator_1_eq));  // open: gt, lt
  and and_1 (signed_overflow, xor_1_out, not_1_out);
  not not_1 (not_1_out, comparator_1_eq);
endmodule
