// Logisim project cpu.circ as structural Verilog: 2 circuits, main circuit main
module main (
  input  [15:0] From_Instr_Mem,
  input  clk,
  output [15:0] r0,
  output [15:0] r1,
  output [15:0] r2,
  output [15:0] r3,
  output [15:0] Display_0,
  output [15:0] Display_1,
  output [15:0] To_Instr_Mem,
  output [15:0] Data_Mem_Data,
  output [15:0] Data_Mem_Addr,
  output Data_Mem_Write
);

  wire addi, ALUSrc, and_1_out, and_2_out, andi, beq, bitselector_1_out, bne, Branch, branch_t, button_1_out,
       disp, equal, extend, jal, jr, Jump, lui, lw, main_2_signed_overflow, not_1_out, not_2_out, not_3_out,
       or_1_out, ori, RegDst, RegWrite, \unsigned ;
  wire [1:0] multiplexer_2_out, multiplexer_4_out;
  wire [2:0] ALUOp;
  wire [3:0] opcode, select;
  wire [5:0] funct;
  wire [7:6] imm;
  wire [11:8] jumpaddr;
  wire [15:0] adder_2_out, bit_extender_1_out, bit_extender_2_out, dIn, imm16, multiplexer_1_out,
       multiplexer_5_out, multiplexer_7_out, multiplexer_8_out, multiplexer_9_out, multiplexer_10_out,
       multiplexer_11_out, multiplexer_14_out, multiplexer_15_out, pc, rr1, rr2, subtractor_1_out,
       subtractor_2_out, write_data;

  Multiplexer #(.width(16)) multiplexer_1 (
    .in0(From_Instr_Mem), .in1(16'h6), .out(multiplexer_1_out), .sel(or_1_out));  // open: en
  or or_1 (or_1_out, branch_t, Jump, jr);
  or or_2 (\unsigned , lui, andi, ori, disp);
  Register #(.width(16)) register_1 (
    .D(multiplexer_1_out), .Q({opcode, jumpaddr, imm, funct}), .clk(clk));  // open: en, clr
  or or_3 (extend, beq, bne, addi, lw, Data_Mem_Write);
  assign bit_extender_1_out = {{8{1'b0}}, {imm, funct}};  // Bit_Extender bit_extender_1
  assign bit_extender_2_out = {{8{imm[7]}}, {imm, funct}};  // Bit_Extender bit_extender_2
  Multiplexer #(.width(2), .enable("false")) multiplexer_2 (
    .in0(jumpaddr[9:8]), .in1(imm), .out(multiplexer_2_out), .sel(RegDst));
  Subtractor #(.width(16)) subtractor_1 (.a(pc), .b(16'h1), .out(subtractor_1_out));  // open: bin, bout
  Register #(.width(16)) u_PC (.D(dIn), .Q(To_Instr_Mem), .clk(clk));  // open: en, clr
  Multiplexer #(.select(3), .width(4)) multiplexer_3 (
    .in0(funct[3:0]), .in1(4'b0001), .in2(4'b0000), .in3(4'b0111), .in4(4'b0110), .in5(4'b0010),
    .out(select), .sel(ALUOp));  // open: in6, in7, en
  Multiplexer #(.width(2), .enable("false")) multiplexer_4 (
    .in0(multiplexer_2_out), .in1(2'b11), .out(multiplexer_4_out), .sel(jal));
  Multiplexer #(.width(16), .enable("false")) multiplexer_5 (
    .in0(write_data), .in1(subtractor_1_out), .out(multiplexer_5_out), .sel(jal));
  Multiplexer #(.width(16), .enable("false")) multiplexer_6 (
    .in0(bit_extender_1_out), .in1(bit_extender_2_out), .out(imm16), .sel(extend));
  Adder #(.width(16)) adder_1 (.a(16'h1), .b(To_Instr_Mem), .out(pc));  // open: cin, cout
  Regfile_main main_1 (
    .Read_register_1(jumpaddr[11:10]), .Read_register_2(jumpaddr[9:8]), .write_register(multiplexer_4_out),
    .write_data(multiplexer_5_out), .Reg_0_Value(r0), .Reg_1_Value(r1), .Reg_2_Value(r2), .Reg_3_Value(r3),
    .RegWrite(RegWrite), .clock(clk), .Read_Data_1(rr1), .Read_Data_2(rr2));
  Adder #(.width(16)) adder_2 (.a(pc), .b(imm16), .out(adder_2_out));  // open: cin, cout
  Multiplexer #(.width(16), .enable("false")) multiplexer_7 (
    .in0(rr1), .in1(imm16), .out(multiplexer_7_out), .sel(lui));
  Multiplexer #(.width(16), .enable("false")) multiplexer_8 (
    .in0(rr2), .in1(imm16), .out(multiplexer_8_out), .sel(ALUSrc));
  Subtractor #(.width(16)) subtractor_2 (.a(adder_2_out), .b(16'h1), .out(subtractor_2_out));  // open: bin, bout
  alu_main main_2 (
    .Switch__S(select), .X(multiplexer_7_out), .Equal(equal), .RESULT(Data_Mem_Addr),
    .Signed_Overflow(main_2_signed_overflow), .Y(multiplexer_9_out));
  Multiplexer #(.width(16), .enable("false")) multiplexer_9 (
    .in0(multiplexer_8_out), .in1(16'h8), .out(multiplexer_9_out), .sel(lui));
  Multiplexer #(.width(16)) multiplexer_10 (
    .in0(pc), .in1(subtractor_2_out), .out(multiplexer_10_out), .sel(branch_t));  // open: en
  RAM #(.addrWidth(16), .dataWidth(16)) ram_1 (
    .addr(Data_Mem_Addr), .data(Data_Mem_Data), .sel(1'b1), .clk(clk), .ld(not_1_out), .clr(button_1_out));
  Button button_1 (.out(button_1_out));
  not not_1 (not_1_out, Data_Mem_Write);
  LED Signed_Overflow (.in(main_2_signed_overflow));
  Multiplexer #(.width(16)) multiplexer_11 (
    .in0(multiplexer_10_out), .in1({pc[15:12], jumpaddr, imm, funct}), .out(multiplexer_11_out), .sel(Jump));  // open: en
  Multiplexer #(.width(16)) multiplexer_12 (.in0(multiplexer_11_out), .in1(rr1), .out(dIn), .sel(jr));  // open: en
  assign Data_Mem_Data = Data_Mem_Write ? rr2 : 16'bz;  // Controlled_Buffer controlled_buffer_1
  Multiplexer #(.width(16), .enable("false")) multiplexer_13 (
    .in0(Data_Mem_Addr), .in1(Data_Mem_Data), .out(write_data), .sel(lw));
  and and_1 (and_1_out, beq, equal);
  and and_2 (and_2_out, bne, not_2_out);
  not not_2 (not_2_out, equal);
  or or_4 (branch_t, and_1_out, and_2_out);
  control control_1 (
    .opcode(opcode), .RegDst(RegDst), .Jump(Jump), .Jr(jr), .ALUSrc(ALUSrc), .RegWrite(RegWrite),
    .Branch(Branch), .ALUOp(ALUOp), .beq(beq), .addi(addi), .andi(andi), .ori(ori), .bne(bne),
    .sw(Data_Mem_Write), .lui(lui), .lw(lw), .disp(disp), .jal(jal));
  Hex_Digit_Display hex_digit_display_1 (.value(Display_0[15:12]));  // open: dp
  Hex_Digit_Display hex_digit_display_2 (.value(Display_0[11:8]));  // open: dp
  Multiplexer #(.width(16), .enable("false")) multiplexer_14 (
    .in0(Display_0), .in1(rr1), .out(multiplexer_14_out), .sel(not_3_out));
  Register #(.width(16)) register_2 (.D(multiplexer_14_out), .en(disp), .Q(Display_0), .clk(clk));  // open: clr
  not not_3 (not_3_out, bitselector_1_out);
  Hex_Digit_Display hex_digit_display_3 (.value(Display_0[3:0]));  // open: dp
  Hex_Digit_Display hex_digit_display_4 (.value(Display_0[7:4]));  // open: dp
  BitSelector #(.width(16)) bitselector_1 (.in(imm16), .out(bitselector_1_out), .sel(4'b0000));
  Hex_Digit_Display hex_digit_display_5 (.value(Display_1[11:8]));  // open: dp
  Hex_Digit_Display hex_digit_display_6 (.value(Display_1[15:12]));  // open: dp
  Hex_Digit_Display hex_digit_display_7 (.value(Display_1[7:4]));  // open: dp
  Hex_Digit_Display hex_digit_display_8 (.value(Display_1[3:0]));  // open: dp
  Register #(.width(16)) register_3 (.D(multiplexer_15_out), .en(disp), .Q(Display_1), .clk(clk));  // open: clr
  Multiplexer #(.width(16), .enable("false")) multiplexer_15 (
    .in0(Display_1), .in1(rr1), .out(multiplexer_15_out), .sel(bitselector_1_out));

  // Other names for the same wires on the sheet: imm[5:0] = funct; jumpaddr[7:0] = {imm, funct};
  //   alu[15:0] = Data_Mem_Addr; branching = branch_t; d0[15:0] = Display_0; d1[15:0] = Display_1;
  //   input[15:0] = From_Instr_Mem; send[15:0] = To_Instr_Mem; sw = Data_Mem_Write

  // Notes on the sheet:
  //   This is the current PC that you need to send as OUTPUT
  //   This is the instruction that you would receive as INPUT
  //   This is a CLK that is an INPUT driven from the harness.
  //   Remember, this circuit is loaded from the harness to be tested!
  //   DO NOT CHANGE THE LOCATIONS OF THE INPUTS OR OUTPUTS! IF YOU DO SO, YOU NEED TO MAKE SURE THE PINS ARE IN THE RIGHT PLACES!
  //   These are OUTPUTS of the circuit
  //   These are OUTPUTS of the circuit
  //   DISPLAY [0]
  //   DISPLAY [1]
endmodule

module control (
  input  [3:0] opcode,
  output RegDst,
  output Jump,
  output Jr,
  output ALUSrc,
  output RegWrite,
  output Branch,
  output [2:0] ALUOp,
  output beq,
  output addi,
  output andi,
  output ori,
  output bne,
  output sw,
  output lui,
  output lw,
  output disp,
  output jal
);

  wire a, b, c, j;

  Demultiplexer #(.select(4), .enable("false")) demultiplexer_1 (
    .out0(RegDst), .out1(jal), .out2(j), .out3(Jr), .out4(beq), .out5(addi), .out6(andi), .out7(ori),
    .out8(bne), .out9(sw), .out10(lui), .out11(lw), .out12(disp), .in(1'b1), .sel(opcode));  // open: out13, out14, out15
  or or_1 (b, bne, beq);
  or or_2 (a, disp, Jr, j, jal, RegDst);
  or or_3 (c, addi, sw, lw);
  assign ALUOp = b ? 3'b001 : 3'bz;  // Controlled_Buffer controlled_buffer_1
  assign ALUOp = c ? 3'b010 : 3'bz;  // Controlled_Buffer controlled_buffer_2
  assign ALUOp = ori ? 3'b100 : 3'bz;  // Controlled_Buffer controlled_buffer_3
  or or_4 (ALUSrc, addi, andi, ori, sw, lui, lw);
  assign ALUOp = a ? 3'b000 : 3'bz;  // Controlled_Buffer controlled_buffer_4
  assign ALUOp = andi ? 3'b011 : 3'bz;  // Controlled_Buffer controlled_buffer_5
  assign ALUOp = lui ? 3'b101 : 3'bz;  // Controlled_Buffer controlled_buffer_6
  or or_5 (Jump, jal, j);
  or or_6 (RegWrite, RegDst, jal, addi, andi, ori, lui, lw);
  or or_7 (Branch, beq, bne);

  // Other names for the same wires on the sheet: Rtype = RegDst
endmodule
